# Fritzing sketch dispenser (saved by Fritzing 0.8.7b)
breadboards: 1

parts:
  VCC = Battery block 9V
  TIP122 = npn-Powertransistor [package="TO220 [THT]"]
  R1 = Resistor [tolerance=±5% resistance=220 package=THT]
  IR_LED = LED - 5mm [color="Infrared (850nm)" package="5 mm [THT]"]
  R2 = Resistor [tolerance=±5% resistance=1k package=THT]
  photo_diode = S1133 Si Photodiode [package="8mm Ceramic [THT]"]
  R3 = Resistor [tolerance=±5% resistance=220 package=THT]
  LED = LED - 5mm [color="Red (633nm)" package="5 mm [THT]"]
  9V_pump = DC Motor
  R4 = Resistor [tolerance=±5% resistance=47k package=THT]

nets:
  N1: VCC.-, TIP122.emitter, IR_LED.cathode, R4.Pin_1
  N2: VCC.+, R1.Pin_1, R2.Pin_1, LED.anode, 9V_pump.pin_1
  N3: TIP122.base, photo_diode.anode, R4.Pin_0
  N4: TIP122.collector, R3.Pin_1, 9V_pump.pin_2
  N5: R1.Pin_0, IR_LED.anode
  N6: R2.Pin_0, photo_diode.cathode
  N7: R3.Pin_0, LED.cathode
