# Fritzing sketch proximity (saved by Fritzing 0.8.7b)
circuit board: 5cm x 5cm
breadboards: 1

parts:
  R3 = Resistor [tolerance=±5% resistance=10k package=THT]
  R2 = Trimmer Potentiometer [maximum_resistance=100kΩ package=THT]
  IC = 555 Timer [package="SO8 [SMD]"]
  C1 = Electrolytic Capacitor [capacitance=10µF package="100 mil [THT, electrolytic]"]
  R1 = Resistor [tolerance=±5% resistance=47k package=THT]
  IR_LED = LED - 5mm [color="Infrared (850nm)" package="5 mm [THT]"]
  R4 = Trimmer Potentiometer [maximum_resistance=10kΩ package=THT]
  R5 = Resistor [tolerance=±5% resistance=220 package=THT]
  photo_diode = S1133 Si Photodiode [package="8mm Ceramic [THT]"]
  LED1 = LED - 5mm [color="Red (633nm)" package="5 mm [THT]"]
  BC547 = NPN-Transistor [package="TO92 [THT]"]
  VCC = Battery block 9V
  9V_pump = DC Motor

nets (from the breadboard view):
  N1: R3.Pin_0, R4.wiper
  N2: R3.Pin_1, IC.Pin_4, IC.Pin_8, R1.Pin_1, R5.Pin_0, VCC.+, 9V_pump.pin_1
  N3: R2.leg1, IC.Pin_6, IC.Pin_7, C1.+
  N4: R2.wiper, R1.Pin_0
  N5: IC.Pin_1, C1.-, IR_LED.cathode, photo_diode.anode, BC547.E, VCC.-
  N6: IC.Pin_2, R4.leg1, photo_diode.cathode
  N7: IC.Pin_3, LED1.anode
  N8: IR_LED.anode, R5.Pin_1
  N9: LED1.cathode, BC547.B
  N10: BC547.C, 9V_pump.pin_2
